# Fritzing sketch Breadboard (saved by Fritzing 0.9.3b)
breadboards: 1

parts:
  NEOPIXEL1 = Neopixel Strip -- White (30/m)
  NEOPIXEL2 = Neopixel Strip -- White (30/m)
  NEOPIXEL4 = Neopixel Strip -- White (30/m)
  NEOPIXEL7 = Neopixel Strip -- White (30/m)
  NEOPIXEL8 = Neopixel Strip -- White (30/m)
  NEOPIXEL9 = Neopixel Strip -- White (30/m)
  NEOPIXEL10 = Neopixel Strip -- White (30/m)
  NEOPIXEL11 = Neopixel Strip -- White (30/m)
  Part1 = Arduino Uno (Rev3)
  Power_plug1 = Power plug
  NEOPIXEL12 = Neopixel Strip -- White (30/m)
  C1 = Electrolytic Capacitor [capacitance=1µF package="100 mil [THT, electrolytic]"]
  R1 = Resistor [tolerance=±5% resistance=220 package=THT]

nets:
  GND: NEOPIXEL1.GND#1, Part1.GND, Power_plug1.GND, NEOPIXEL12.GND#6, C1.-
  N1: NEOPIXEL1.Din, R1.Pin_0
  5V: NEOPIXEL1.+5V#3, Part1.5V, Power_plug1.VCC, NEOPIXEL12.+5V#4, C1.+
  N2: NEOPIXEL1.+5V#4, NEOPIXEL2.+5V#3
  N3: NEOPIXEL1.Dout, NEOPIXEL2.Din
  N4: NEOPIXEL1.GND#6, NEOPIXEL2.GND#1
  N5: NEOPIXEL2.+5V#4, NEOPIXEL4.+5V#3
  N6: NEOPIXEL2.Dout, NEOPIXEL4.Din
  N7: NEOPIXEL2.GND#6, NEOPIXEL4.GND#1
  N8: NEOPIXEL4.+5V#4, NEOPIXEL8.+5V#3
  N9: NEOPIXEL4.Dout, NEOPIXEL8.Din
  N10: NEOPIXEL4.GND#6, NEOPIXEL8.GND#1
  N11: NEOPIXEL7.GND#1, NEOPIXEL8.GND#6
  N12: NEOPIXEL7.Din, NEOPIXEL8.Dout
  N13: NEOPIXEL7.+5V#3, NEOPIXEL8.+5V#4
  N14: NEOPIXEL7.+5V#4, NEOPIXEL10.+5V#3
  N15: NEOPIXEL7.Dout, NEOPIXEL10.Din
  N16: NEOPIXEL7.GND#6, NEOPIXEL10.GND#1
  N17: NEOPIXEL9.GND#1, NEOPIXEL10.GND#6
  N18: NEOPIXEL9.Din, NEOPIXEL10.Dout
  N19: NEOPIXEL9.+5V#3, NEOPIXEL10.+5V#4
  N20: NEOPIXEL9.+5V#4, NEOPIXEL11.+5V#3
  N21: NEOPIXEL9.Dout, NEOPIXEL11.Din
  N22: NEOPIXEL9.GND#6, NEOPIXEL11.GND#1
  N23: NEOPIXEL11.+5V#4, NEOPIXEL12.+5V#3
  N24: NEOPIXEL11.Dout, NEOPIXEL12.Din
  N25: NEOPIXEL11.GND#6, NEOPIXEL12.GND#1
  N26: Part1.D6_PWM, R1.Pin_1

notes:
  5V
  29 LEDs per Row
  Serial

custom parts:
  Neopixel Strip -- White (30/m): These NeoPixel strips have 30 digitally-addressable pixel LEDs per meter and are very affordable and are only 12.5 mm wide, 10 mm if you remove the strip from the casing.
